// Logisim project 8BitALU+Tablo.circ as structural Verilog: 3 circuits, main circuit main
module main (
  input  Cin,
  input  [1:0] OP,
  input  B1S,
  input  A1S,
  input  in_5,
  input  [7:0] A,
  input  [7:0] B,
  output [7:0] Output,
  output zero,
  output Over_Flow
);

  wire n1_bit_alu_1_overflow, n1_bit_alu_2_overflow, n1_bit_alu_3_overflow, n1_bit_alu_4_overflow,
       n1_bit_alu_5_overflow, n1_bit_alu_6_overflow, n1_bit_alu_7_overflow, or_1_out, xor_1_out;

  xor xor_1 (xor_1_out, Over_Flow, Output[7]);
  _1_Bit_Alu u_1_bit_alu_1 (
    .Cin(Cin), .Op(OP), .Binv(B1S), .Ainv(A1S), .A(A[0]), .B(B[0]), .SLT(xor_1_out), .Y(Output[0]),
    .OverFlow(n1_bit_alu_1_overflow));
  _1_Bit_Alu u_1_bit_alu_2 (
    .Cin(n1_bit_alu_1_overflow), .Op(OP), .Binv(B1S), .Ainv(A1S), .A(A[1]), .B(B[1]), .SLT(in_5),
    .Y(Output[1]), .OverFlow(n1_bit_alu_2_overflow));
  _1_Bit_Alu u_1_bit_alu_3 (
    .Cin(n1_bit_alu_2_overflow), .Op(OP), .Binv(B1S), .Ainv(A1S), .A(A[2]), .B(B[2]), .SLT(in_5),
    .Y(Output[2]), .OverFlow(n1_bit_alu_3_overflow));
  _1_Bit_Alu u_1_bit_alu_4 (
    .Cin(n1_bit_alu_3_overflow), .Op(OP), .Binv(B1S), .Ainv(A1S), .A(A[3]), .B(B[3]), .SLT(in_5),
    .Y(Output[3]), .OverFlow(n1_bit_alu_4_overflow));
  _1_Bit_Alu u_1_bit_alu_5 (
    .Cin(n1_bit_alu_4_overflow), .Op(OP), .Binv(B1S), .Ainv(A1S), .A(A[4]), .B(B[4]), .SLT(in_5),
    .Y(Output[4]), .OverFlow(n1_bit_alu_5_overflow));
  _1_Bit_Alu u_1_bit_alu_6 (
    .Cin(n1_bit_alu_5_overflow), .Op(OP), .Binv(B1S), .Ainv(A1S), .A(A[5]), .B(B[5]), .SLT(in_5),
    .Y(Output[5]), .OverFlow(n1_bit_alu_6_overflow));
  _1_Bit_Alu u_1_bit_alu_7 (
    .Cin(n1_bit_alu_6_overflow), .Op(OP), .Binv(B1S), .Ainv(A1S), .A(A[6]), .B(B[6]), .SLT(in_5),
    .Y(Output[6]), .OverFlow(n1_bit_alu_7_overflow));
  _1_Bit_Alu u_1_bit_alu_8 (
    .Cin(n1_bit_alu_7_overflow), .Op(OP), .Binv(B1S), .Ainv(A1S), .A(A[7]), .B(B[7]), .SLT(in_5),
    .Y(Output[7]), .OverFlow(Over_Flow));
  or or_1 (or_1_out, Output[0], Output[1], Output[2], Output[3], Output[4], Output[5], Output[6], Output[7]);
  not not_1 (zero, or_1_out);

  // Notes on the sheet:
  //   8 bit Arithmetic and Logic Unit
  //   Process
  //   Adder
  //   Subtractor
  //   AND
  //   OR
  //   OP
  //   10
  //   10
  //   00
  //   01
  //   B1S
  //   Function
  //   --------------------------------------------------------------------------------------
  //   --------------------------------------------------------------------------------------
  //   +   Cin
  //   --------------------------------------------------------------------------------------
  //   --------------------------------------------------------------------------------------
endmodule

// +
module _1_bit_adder (
  input  a,
  input  b,
  input  Cin,
  output Sum,
  output Cout
);

  wire and_1_out, and_2_out, xor_1_out;

  xor xor_1 (xor_1_out, a, b);
  and and_1 (and_1_out, a, b);
  xor xor_2 (Sum, xor_1_out, Cin);
  and and_2 (and_2_out, xor_1_out, Cin);
  or or_1 (Cout, and_2_out, and_1_out);
endmodule

module _1_Bit_Alu (
  input  Cin,
  input  [1:0] Op,
  input  Binv,
  input  Ainv,
  input  A,
  input  B,
  input  SLT,
  output Y,
  output OverFlow
);

  wire and_1_out, multiplexer_1_out, multiplexer_2_out, n1_bit_adder_1_sum, not_1_out, not_2_out, or_1_out;

  not not_1 (not_1_out, A);
  not not_2 (not_2_out, B);
  Multiplexer #(.enable("false")) multiplexer_1 (.in0(A), .in1(not_1_out), .out(multiplexer_1_out), .sel(Ainv));
  Multiplexer #(.enable("false")) multiplexer_2 (.in0(B), .in1(not_2_out), .out(multiplexer_2_out), .sel(Binv));
  and and_1 (and_1_out, multiplexer_1_out, multiplexer_2_out);
  or or_1 (or_1_out, multiplexer_1_out, multiplexer_2_out);
  _1_bit_adder u_1_bit_adder_1 (
    .a(multiplexer_1_out), .b(multiplexer_2_out), .Cin(Cin), .Sum(n1_bit_adder_1_sum), .Cout(OverFlow));
  Multiplexer #(.select(2), .disabled(0), .enable("false")) multiplexer_3 (
    .in0(and_1_out), .in1(or_1_out), .in2(n1_bit_adder_1_sum), .in3(SLT), .out(Y), .sel(Op));

  // Notes on the sheet:
  //   1 Bit ALU
endmodule
